# Fritzing sketch robot (saved by Fritzing 0.9.6b)
breadboards: 1

parts:
  Arduino_Nano_Every = Arduino Nano Every
  +V5 = Camdenboss CTB0158-2 [part_number=CTB0158/2 package=THT]
  V_motor = Camdenboss CTB0158-2 [part_number=CTB0158/2 package=THT]
  Motor_Driver = Adafruit TB6612 DC and Stepper Motor Driver [part_number=TB6612]
  L_Motor = Camdenboss CTB0158-2 [part_number=CTB0158/2 package=THT]
  R_Motor = Camdenboss CTB0158-2 [part_number=CTB0158/2 package=THT]
  HMC5883L = Boladge HMC5883L Compass Module
  C1 = Ceramic Capacitor [capacitance=100nF voltage=35V package="1206 [SMD, multilayer]"]
  C2 = Ceramic Capacitor [capacitance=100nF voltage=35V package="1206 [SMD, multilayer]"]
  C3 = Ceramic Capacitor [capacitance=100nF voltage=35V package="1206 [SMD, multilayer]"]
  C4 = Ceramic Capacitor [capacitance=100nF voltage=35V package="1206 [SMD, multilayer]"]
  Rotary_Enc = Camdenboss CTB0158-2 [part_number=CTB0158/2 package=THT]
  Piezo = Piezo Speaker
  HC-SR04 = HC-SR04 Ultrasonic Distance Sensor

nets:
  GND: Arduino_Nano_Every.GND, Arduino_Nano_Every.D13~, +V5.pin2, V_motor.pin2, Motor_Driver.GND, HMC5883L.GND, C3.0, C4.0, Piezo.pin1, HC-SR04.GND
  N1: Arduino_Nano_Every.D2, Motor_Driver.AIN2
  N2: Arduino_Nano_Every.D4, Motor_Driver.AIN1
  N3: Arduino_Nano_Every.D7, Motor_Driver.BIN1
  N4: Arduino_Nano_Every.D8, Motor_Driver.BIN2
  N5: Arduino_Nano_Every.D9~, Motor_Driver.PWMA
  N6: Arduino_Nano_Every.D10~, Motor_Driver.PWMB
  VCC: Arduino_Nano_Every.D11/MOSI, Arduino_Nano_Every.+5V, +V5.pin1, Motor_Driver.VCC, HMC5883L.VCC, HC-SR04.VCC, HC-SR04.TRIG
  N7: Arduino_Nano_Every.D12~/MISO, HC-SR04.ECHO
  N8: Arduino_Nano_Every.A6, C4.1, Rotary_Enc.pin1
  N9: Arduino_Nano_Every.A5, HMC5883L.SCL
  N10: Arduino_Nano_Every.A4, HMC5883L.SDA
  N11: Arduino_Nano_Every.A3, Piezo.pin2
  N12: Arduino_Nano_Every.A7, C3.1, Rotary_Enc.pin2
  N13: V_motor.pin1, Motor_Driver.Vmotor, Motor_Driver.PWRIN
  N14: Motor_Driver.MOTORA1, R_Motor.pin1, C2.1
  N15: Motor_Driver.MOTORA2, R_Motor.pin2, C2.0
  N16: Motor_Driver.MOTORB2, L_Motor.pin2, C1.0
  N17: Motor_Driver.MOTORB1, L_Motor.pin1, C1.1

custom parts:
  Arduino Nano Every: The Nano Every is Arduino’s 5V compatible board in the smallest available form factor: 45x18mm! The Arduino Nano is the preferred board for many projects requiring a small and easy to use microcontroller board. The small footprint and low price, make the Nano Every particularly suited for wearable inventions, low cost robotics, electronic musical instruments, and general use to control smaller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
  Adafruit TB6612 DC and Stepper Motor Driver: Spin two DC motors, step one bi-polar or uni-polar stepper, or fire off two solenoids with 1.2A per channel using the TB6612. These are perhaps better known as "the drivers in our assembled Adafruit Motorshield or Motor HAT." We really like these dual H-bridges, so if you want to control motors without a shield or HAT these are easy to include on any solderless breadboard or perma-proto.
  Boladge HMC5883L Compass Module: Cheap digital compass module
